# Fritzing sketch FrankenFender (saved by Fritzing 1.0.3b)
perfboards: 1

parts:
  J1 = female pin header, 2 pins [form="♀ (female)"]
  Bela1 = Bela Mini
  J2 = female pin header, 3 pins [form="♀ (female)"]
  J3 = female pin header, 3 pins [form="♀ (female)"]
  R1 = Resistor [tolerance=±5% power=0.25W resistance=220 package=THT]
  R2 = Resistor [tolerance=±5% power=0.25W resistance=220 package=THT]
  J4 = male pin header, 5 pins [form="♂ (male)"]
  C1 = Ceramic Capacitor [capacitance=100nF voltage=35V package="200 mil [THT, multilayer]"]
  M1 = mic-test [package=THT]
  M2 = mic-test [package=THT]
  R3 = Rotary Potentiometer (Small) [maximum_resistance=10kΩ knob_status=50% power=0.5W package=THT]
  R4 = Rotary Potentiometer (Small) [maximum_resistance=10kΩ knob_status=50% power=0.5W package=THT]
  R5 = Rotary Potentiometer (Small) [maximum_resistance=10kΩ knob_status=50% power=0.5W package=THT]

nets:
  N1: J1.pin1, R1.Pin_0, R2.Pin_0, C1.0, C1.1, R3.leg1, R4.leg1, R5.leg1
  N2: J1.pin2, Bela1.GND, J3.pin3, J4.pin5, M1.pin1, M2.pin1, R3.leg2, R4.leg2, R5.leg2
  N3: Bela1.3.3V, J4.pin1
  N4: Bela1.A0, J2.pin1, J4.pin2, R3.wiper
  N5: Bela1.A1, J2.pin2, J4.pin3, R4.wiper
  N6: Bela1.A2, J2.pin3, J4.pin4, R5.wiper
  N7: Bela1.AUDIO_IN_L, J3.pin1, J3.pin2, M1.pin3, M2.pin3
  N8: R1.Pin_1, R2.Pin_1

custom parts:
  Bela Mini: Bela Mini Fritzing part, including PCB schematic
  mic-test: Test part to see if gradiants work.
